# Fritzing sketch untested_arduino_standalone (saved by Fritzing 0.7.1b)
breadboards: 1

parts:
  U1 = atmega328 [package=dip]
  U2 = Voltage Regulator - 5V [package="DPak [SMD]"]
  LED1 = LED - 3mm [color="Red (633nm)" package="3 mm [THT]"]
  R2 = Resistor [tolerance=±5% resistance=220 package=THT]
  R3 = Resistor [tolerance=±5% resistance=10k package=THT]
  C1 = Electrolytic Capacitor [capacitance=10µF package="100 mil [THT, electrolytic]"]
  C2 = Electrolytic Capacitor [capacitance=10µF package="100 mil [THT, electrolytic]"]
  XTAL2 = Crystal [frequency="16 Mhz" package=THT]
  C4 = Tantalum Capacitor [capacitance=22pF package="100 mil [THT, tantalum]"]
  C5 = Tantalum Capacitor [capacitance=22pF package="100 mil [THT, tantalum]"]
  S1 = Pushbutton [package="[THT]"]

nets:
  N1: U1.RESET, R3.Pin_0, S1.Pin_1, S1.Pin_2
  N2: U1.VCC, U1.AVCC, U1.AREF, U2.output_voltage, R2.Pin_1, R3.Pin_1, C1.+
  GND: U1.GND, U2.GND, LED1.cathode, C1.-, C2.-, C4.+, C5.+, S1.Pin_3, S1.Pin_4
  N3: U1.XLAT1, XTAL2.pin_0, C5.-
  N4: U1.XLAT2, XTAL2.pin_1, C4.-
  N5: U2.input_voltage, C2.+
  N6: LED1.anode, R2.Pin_0
