# Fritzing sketch 4relays_module (saved by Fritzing 0.7.4b)

parts:
  ATMega_Power2 = Power plug
  Part1 = Relay T73
  J18 = Screw terminal - 2 pins [package=THT]
  J19 = Screw terminal - 2 pins [package=THT]
  J20 = Screw terminal - 2 pins [package=THT]
  J21 = Screw terminal - 2 pins [package=THT]
  Part2 = Relay T73
  Part3 = Relay T73
  Part4 = Relay T73
  J22 = male pin header, 5 pins [form="♂ (male)"]

nets:
  N1: ATMega_Power2.GND, J18.pin2, J19.pin2, J20.pin2, J21.pin2
  N2: ATMega_Power2.VCC, Part1.COM, Part2.COM, Part3.COM, Part4.COM
  N3: Part1.C1, Part2.C1, Part3.C1, Part4.C1, J22.pin5
  N4: Part1.C2, J22.pin1
  N5: Part1.NO, J18.pin1
  N6: J19.pin1, Part2.NO
  N7: J20.pin1, Part3.NO
  N8: J21.pin1, Part4.NO
  N9: Part2.C2, J22.pin2
  N10: Part3.C2, J22.pin3
  N11: Part4.C2, J22.pin4

custom parts:
  Relay T73: An T73 Mini PCB Relay
