# Fritzing sketch simple_garden_watering (saved by Fritzing 0.7.4b)
breadboards: 2

parts:
  K1 = Relay [part_number=FRS1B-S package=THT]
  K2 = Relay [part_number=FRS1B-S package=THT]
  K3 = Relay [part_number=FRS1B-S package=THT]
  K4 = Relay [part_number=FRS1B-S package=THT]
  K5 = Relay [part_number=FRS1B-S package=THT]
  K6 = Relay [part_number=FRS1B-S package=THT]
  K7 = Relay [part_number=FRS1B-S package=THT]
  K8 = Relay [part_number=FRS1B-S package=THT]
  J1 = Screw terminal - 2 pins [package=THT]
  J2 = Screw terminal - 2 pins [package=THT]
  J3 = Screw terminal - 2 pins [package=THT]
  J4 = Screw terminal - 2 pins [package=THT]
  J5 = Screw terminal - 2 pins [package=THT]
  J6 = Screw terminal - 2 pins [package=THT]
  J7 = Screw terminal - 2 pins [package=THT]
  J8 = Screw terminal - 2 pins [package=THT]
  Solenoid_Valves_Power = Power plug
  U1 = atmega328 [package=dip]
  C1 = Electrolytic Capacitor [capacitance=10µF voltage=20V package="100 mil [THT, electrolytic]"]
  C2 = Electrolytic Capacitor [capacitance=10µF voltage=20V package="100 mil [THT, electrolytic]"]
  U2 = Voltage Regulator - 5V [package="TO220 [THT]"]
  ATMega_Power = Power plug
  S1 = Pushbutton [package="[THT]"]
  R1 = Resistor [tolerance=±5% resistance=10k package="0603 [SMD]"]
  J9 = male pin header, 4 pins [form="♂ (male)"]

nets:
  N1: K1.COIL1, U1.D5_(PWM)
  N2: K1.C1, K1.C2, K2.C1, K2.C2, K3.C1, K3.C2, K4.C1, K4.C2, K5.C1, K5.C2, K6.C1, K6.C2, K7.C1, K7.C2, K8.C1, K8.C2, Solenoid_Valves_Power.VCC
  N3: K1.COIL2, K2.COIL2, K3.COIL2, K4.COIL2, K5.COIL2, K6.COIL2, K7.COIL2, K8.COIL2
  N4: K1.B, J1.pin1
  N5: K2.COIL1, U1.D6_(PWM)
  N6: K2.B, J2.pin1
  N7: K3.COIL1, U1.D7
  N8: K3.B, J3.pin1
  N9: K4.COIL1, U1.D8
  N10: K4.B, J4.pin1
  N11: K5.COIL1, U1.D9_(PWM)
  N12: K5.B, J5.pin1
  N13: K6.COIL1, U1.D10_(PWM)
  N14: K6.B, J6.pin1
  N15: K7.COIL1, U1.D11_(PWM)
  N16: K7.B, J7.pin1
  N17: K8.COIL1, U1.D12
  N18: K8.B, J8.pin1
  N19: J1.pin2, J2.pin2, J3.pin2, J4.pin2, J5.pin2, J6.pin2, J7.pin2, J8.pin2, Solenoid_Valves_Power.GND
  N20: U1.RESET, S1.Pin_1, S1.Pin_2, R1.Pin_0
  N21: U1.D0_(RX), J9.pin4
  N22: U1.D1_(TX), J9.pin3
  N23: U1.VCC, C1.+, U2.output_voltage, R1.Pin_1, J9.pin2
  GND: U1.GND, C1.-, C2.-, U2.GND, ATMega_Power.GND, S1.Pin_3, S1.Pin_4, J9.pin1
  N24: C2.+, U2.input_voltage, ATMega_Power.VCC
